// Logisim project Mini_Project.circ as structural Verilog: 2 circuits, main circuit main
module main (
);

  wire ALU_MUX, CLK, decoder_1_out8, decoder_1_out9, decoder_1_out10, decoder_1_out11, decoder_1_out12,
       decoder_1_out13, decoder_1_out14, decoder_1_out15, IC_carry, IR_WE, LOAD_PC, PC_EN, R0_WE, R1_WE,
       R2_OE, R2_WE, RAM_IE, RAM_OE, RES_IC, RES_IR, SP_OE, SP_WE, undriven, undriven_2, undriven_3;
  wire [3:0] IC_q, undriven_4;
  wire [7:0] alu_1_out_4, controlled_buffer_1_out, decoder_1_out0, IR_q, multiplexer_1_out,
       multiplexer_2_out, PC_q, R0_q, R1_q, R2_q, ram_1_dout, SP_q;
  wire [13:0] PLA_Decoder_out;

  Multiplexer #(.width(8)) multiplexer_1 (.in0(ram_1_dout), .in1(R2_q), .out(multiplexer_1_out), .sel(R2_OE));
  Register #(.trigger("falling")) R0 (.D(multiplexer_1_out), .en(R0_WE), .clk(CLK), .Q(R0_q), .clr(undriven));
  Register #(.trigger("falling")) R1 (.D(multiplexer_1_out), .en(R1_WE), .clk(CLK), .Q(R1_q), .clr(undriven_2));
  // NoConnect on undriven
  // NoConnect on undriven_2
  ALU alu_1 (.a(R0_q), .b(R1_q), .sel(ALU_MUX), .out_4(alu_1_out_4));
  Register #(.trigger("falling")) R2 (.D(alu_1_out_4), .en(R2_WE), .clk(CLK), .Q(R2_q), .clr(undriven_3));
  // NoConnect on undriven_3
  RAM ram_1 (.addr(PC_q), .we(RAM_IE), .oe(RAM_OE), .clk(CLK), .din(R2_q), .dout(ram_1_dout));
  Register #(.trigger("falling")) IR (.D(ram_1_dout), .en(IR_WE), .clk(CLK), .Q(IR_q), .clr(RES_IR));
  Multiplexer #(.width(8)) multiplexer_2 (
    .in0(ram_1_dout), .in1(controlled_buffer_1_out), .out(multiplexer_2_out), .sel(SP_OE));
  Clock clock_1 (.out(CLK));
  // NoConnect on IR_q[7:4]
  Counter #(.trigger("falling")) PC (
    .clr(1'b0), .load(LOAD_PC), .up(1'b1), .count(PC_EN), .clk(CLK), .D(multiplexer_2_out), .Q(PC_q));  // open: carry
  Register #(.trigger("falling")) SP (.D(PC_q), .en(SP_WE), .clk(CLK), .Q(SP_q));  // open: clr
  assign controlled_buffer_1_out = SP_OE ? SP_q : 8'bz;  // Controlled_Buffer controlled_buffer_1
  Counter #(.max('hf), .trigger("falling"), .width(4)) IC (
    .clr(RES_IC), .load(1'b0), .up(1'b1), .count(1'b1), .clk(CLK), .D(undriven_4), .carry(IC_carry), .Q(IC_q));
  // NoConnect on undriven_4
  // NoConnect on decoder_1_out8
  // NoConnect on decoder_1_out9
  // NoConnect on decoder_1_out10
  // NoConnect on decoder_1_out11
  // NoConnect on decoder_1_out12
  // NoConnect on decoder_1_out13
  // NoConnect on decoder_1_out14
  // NoConnect on decoder_1_out15
  Decoder #(.enable("false"), .select(4)) decoder_1 (
    .out0(decoder_1_out0[0]), .out1(decoder_1_out0[1]), .out2(decoder_1_out0[2]), .out3(decoder_1_out0[3]),
    .out4(decoder_1_out0[4]), .out5(decoder_1_out0[5]), .out6(decoder_1_out0[6]), .out7(decoder_1_out0[7]),
    .out8(decoder_1_out8), .out9(decoder_1_out9), .out10(decoder_1_out10), .out11(decoder_1_out11),
    .out12(decoder_1_out12), .out13(decoder_1_out13), .out14(decoder_1_out14), .out15(decoder_1_out15),
    .sel(IC_q));
  // NoConnect on IC_carry
  PLA #(.in_width(12), .out_width(14), .\table ("000000010000 00000000000110 # Initial_Fetech\n000000100001 00000000001000 # ADD_1\n000001000001 00111000000000 # ADD_2\n000000100010 00000010001000 # AND_1\n000001000010 00111000000000 # AND_2\n000000100011 00000001010000 # COPY_R1_1\n000001000011 00111000000000 # COPY_R1_2\n000000100100 00000000110000 # COPY_R0_1\n000001000100 00111000000000 # COPY_R0_2\n000000100101 00001000000000 # READ_R0_1\n000001000101 00000000100010 # READ_R0_2\n000010000101 00111000000000 # READ_R0_3\n000000100110 00001000000000 # READ_R1_1\n000001000110 00000001000010 # READ_R1_2\n000010000110 00111000000000 # READ_R1_3\n000000100111 00001000000000 # JUMP_1\n000001000111 00001100000010 # JUMP_2\n000010000111 00110000000000 # JUMP_3\n000000101000 00001000000000\n000001001000 01000000000000\n000010001000 00001100000010\n000100001000 00000000010001\n001000001000 10001100000000\n010000001000 00001000000000\n100000001000 00110000000000\n000000010001 00000000000110\n000000010010 00000000000110\n000000010011 00000000000110\n000000010100 00000000000110\n000000010101 00000000000110\n000000010110 00000000000110\n000000010111 00000000000110\n000000011000 00000000000110")) PLA_Decoder (
    .in({decoder_1_out0, IR_q[3:0]}), .out({PLA_Decoder_out[13:2], RAM_OE, PLA_Decoder_out[0]}));
  D_Flip_Flop d_ff_1 (.D(PLA_Decoder_out[0]), .clk(CLK), .Q(RAM_IE));  // open: Qn, preset, reset
  D_Flip_Flop d_ff_2 (.D(PLA_Decoder_out[2]), .clk(CLK), .Q(IR_WE));  // open: Qn, preset, reset
  D_Flip_Flop d_ff_3 (.D(PLA_Decoder_out[3]), .clk(CLK), .Q(R2_WE));  // open: Qn, preset, reset
  D_Flip_Flop d_ff_4 (.D(PLA_Decoder_out[4]), .clk(CLK), .Q(R2_OE));  // open: Qn, preset, reset
  D_Flip_Flop d_ff_5 (.D(PLA_Decoder_out[5]), .clk(CLK), .Q(R0_WE));  // open: Qn, preset, reset
  D_Flip_Flop d_ff_6 (.D(PLA_Decoder_out[6]), .clk(CLK), .Q(R1_WE));  // open: Qn, preset, reset
  D_Flip_Flop d_ff_7 (.D(PLA_Decoder_out[7]), .clk(CLK), .Q(ALU_MUX));  // open: Qn, preset, reset
  D_Flip_Flop d_ff_8 (.D(PLA_Decoder_out[8]), .clk(CLK), .Q(LOAD_PC));  // open: Qn, preset, reset
  D_Flip_Flop d_ff_9 (.D(PLA_Decoder_out[9]), .clk(CLK), .Q(PC_EN));  // open: Qn, preset, reset
  D_Flip_Flop d_ff_10 (.D(PLA_Decoder_out[10]), .clk(CLK), .Q(RES_IC));  // open: Qn, preset, reset
  D_Flip_Flop d_ff_11 (.D(PLA_Decoder_out[11]), .clk(CLK), .Q(RES_IR));  // open: Qn, preset, reset
  D_Flip_Flop d_ff_12 (.D(PLA_Decoder_out[12]), .clk(CLK), .Q(SP_WE));  // open: Qn, preset, reset
  D_Flip_Flop d_ff_13 (.D(PLA_Decoder_out[13]), .clk(CLK), .Q(SP_OE));  // open: Qn, preset, reset
endmodule

module ALU (
  input  [7:0] a,
  input  [7:0] b,
  input  sel,
  output [7:0] out_4
);

  wire [7:0] adder_1_out, AND_ALU_out;

  Adder adder_1 (.a(a), .b(b), .out(adder_1_out));  // open: cin, cout
  assign AND_ALU_out = a & b;  // AND_Gate AND_ALU, 8 bits wide
  Multiplexer #(.width(8)) multiplexer_1 (.in0(adder_1_out), .in1(AND_ALU_out), .out(out_4), .sel(sel));
endmodule
